# Fritzing sketch fritzing (saved by Fritzing 1.0.4)
breadboards: 1

parts:
  Part1 = Arduino Nano (Rev3.0)  # not connected
  MCU1 = Raspberry Pi Zero
  VCC1 = 4 x AAA Battery Mount [internal_resistance=0.1Ω]
  KF-1 = KF-301 Relay [package=THT]
  Capacitive_Soil_Moisture_Sensor1 = DFRobot Capacitive Soil Moisture Sensor V1.0 [part_number=SEN0193]  # not connected
  Mini_Water_Pump_3-6VDC1 = Mini Water Pump 3-6VDC [part_number="Mini Water Pump 3-6VDC" chip_label=IC package="DIP (Dual Inline) [THT]"]

nets:
  N1: MCU1.pin_2, MCU1.pin_4, KF-1.power
  N2: MCU1.pin_6, MCU1.pin_20, KF-1.ground
  N3: MCU1.pin_13, KF-1.signal
  N4: VCC1.-, Mini_Water_Pump_3-6VDC1.-M
  N5: VCC1.+, KF-1.NO
  N6: KF-1.C, Mini_Water_Pump_3-6VDC1.+M

notes:
  Arduino nano is connected to the laptop via usb

custom parts:
  KF-301 Relay: KF-301
  DFRobot Capacitive Soil Moisture Sensor V1.0: DFRobot Capacitive Soil Moisture Sensor V1.0 This product measures soil moisture levels by capacitive sensing, rather than resistive sensing like other types of moisture sensor. It is made of a corrosion resistant material giving it a long service life. Insert it into soil and impress your friends with the real-time soil moisture data! The product includes an on-board voltage regulator which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
